// Logisim project Stack.circ as structural Verilog: 1 circuit, main circuit main
module main (
  input  PUSH,
  input  [1:0] in_2,
  input  POP,
  input  in_4,
  output [1:0] out_5
);

  wire and_1_out, clock_1_out;
  wire [7:0] counter_1_q;

  and and_1 (and_1_out, POP, PUSH);
  Clock clock_1 (.out(clock_1_out));
  Counter counter_1 (.load(POP), .count(and_1_out), .Q(counter_1_q), .clk(clock_1_out));  // open: D, carry, clr
  RAM #(.dataWidth(2), .bus("separate")) ram_1 (
    .addr(counter_1_q), .din(in_2), .data(out_5), .str(PUSH), .clk(clock_1_out));  // open: sel, ld, clr
endmodule
